# Fritzing sketch CUNO (saved by Fritzing 0.9.5d)

parts:
  WeMos_D1_Mini1 = WeMos D1 Mini
  U1 = CC1101 [part_number=CC1101]

nets:
  N1: WeMos_D1_Mini1.3V3, U1.1
  N2: WeMos_D1_Mini1.D1, U1.6
  N3: WeMos_D1_Mini1.D2, U1.7
  N4: WeMos_D1_Mini1.D5, U1.4
  N5: WeMos_D1_Mini1.D6, U1.5
  N6: WeMos_D1_Mini1.D7, U1.3
  N7: WeMos_D1_Mini1.D8, U1.8
  N8: WeMos_D1_Mini1.G, U1.2
  N9: U1.10, U1.11
